// Logisim project Project_3.circ as structural Verilog: 7 circuits, main circuit main
module main (
  input  in_1
);

  wire base_10_to_base_6_counter_1_out_2, base_10_to_base_6_counter_1_out_3,
       base_10_to_base_6_counter_1_out_4, base_10_to_base_6_counter_1_out_5,
       base_10_to_base_6_counter_1_out_6, base_10_to_base_6_counter_1_out_7,
       base_10_to_base_6_counter_1_out_8, base_10_to_base_6_counter_1_out_9, n7_segment_display_driver_1_p5,
       n7_segment_display_driver_1_p6, n7_segment_display_driver_1_p7, n7_segment_display_driver_1_p8,
       n7_segment_display_driver_1_p9, n7_segment_display_driver_1_p10, n7_segment_display_driver_1_p11,
       n7_segment_display_driver_2_p5, n7_segment_display_driver_2_p6, n7_segment_display_driver_2_p7,
       n7_segment_display_driver_2_p8, n7_segment_display_driver_2_p9, n7_segment_display_driver_2_p10,
       n7_segment_display_driver_2_p11;

  base_10_to_base_6_counter base_10_to_base_6_counter_1 (
    .in_1(in_1), .out_2(base_10_to_base_6_counter_1_out_2), .out_4(base_10_to_base_6_counter_1_out_4),
    .out_6(base_10_to_base_6_counter_1_out_6), .out_7(base_10_to_base_6_counter_1_out_7),
    .out_5(base_10_to_base_6_counter_1_out_5), .out_8(base_10_to_base_6_counter_1_out_8),
    .out_9(base_10_to_base_6_counter_1_out_9), .out_3(base_10_to_base_6_counter_1_out_3));
  // _7_segment_display_driver 7_segment_display_driver_1: pin names not known; wires that end beside it: base_10_to_base_6_counter_1_out_2, base_10_to_base_6_counter_1_out_4, base_10_to_base_6_counter_1_out_6, base_10_to_base_6_counter_1_out_7, n7_segment_display_driver_1_p5, n7_segment_display_driver_1_p6, n7_segment_display_driver_1_p7, n7_segment_display_driver_1_p8, n7_segment_display_driver_1_p9, n7_segment_display_driver_1_p10, n7_segment_display_driver_1_p11
  _7_Segment_Display u_7_segment_display_1 (
    .g(n7_segment_display_driver_2_p11), .f(n7_segment_display_driver_2_p10),
    .a(n7_segment_display_driver_2_p5), .b(n7_segment_display_driver_2_p6),
    .e(n7_segment_display_driver_2_p9), .d(n7_segment_display_driver_2_p8), .c(n7_segment_display_driver_2_p7));  // open: dp
  _7_Segment_Display u_7_segment_display_2 (
    .g(n7_segment_display_driver_1_p11), .f(n7_segment_display_driver_1_p10),
    .a(n7_segment_display_driver_1_p5), .b(n7_segment_display_driver_1_p6),
    .e(n7_segment_display_driver_1_p9), .d(n7_segment_display_driver_1_p8), .c(n7_segment_display_driver_1_p7));  // open: dp
  // _7_segment_display_driver 7_segment_display_driver_2: pin names not known; wires that end beside it: base_10_to_base_6_counter_1_out_3, base_10_to_base_6_counter_1_out_5, base_10_to_base_6_counter_1_out_8, base_10_to_base_6_counter_1_out_9, n7_segment_display_driver_2_p5, n7_segment_display_driver_2_p6, n7_segment_display_driver_2_p7, n7_segment_display_driver_2_p8, n7_segment_display_driver_2_p9, n7_segment_display_driver_2_p10, n7_segment_display_driver_2_p11
endmodule

module dec_7reg_driver (
  input  A,
  input  B,
  input  C,
  input  D,
  output a_2,
  output b_2,
  output c_2,
  output d_2,
  output e,
  output f,
  output g
);

  wire and_1_out, and_2_out, and_3_out, and_4_out, and_5_out, and_6_out, and_7_out, and_8_out, and_9_out,
       and_10_out, and_11_out, and_12_out, and_13_out, and_14_out, and_15_out, and_16_out, not_1_out,
       not_2_out, not_3_out, not_4_out;

  not not_1 (not_1_out, A);
  not not_2 (not_2_out, B);
  not not_3 (not_3_out, C);
  not not_4 (not_4_out, D);
  and and_1 (and_1_out, not_4_out, not_2_out);
  and and_2 (and_2_out, B, D);
  and and_3 (and_3_out, not_3_out, not_4_out);
  and and_4 (and_4_out, not_2_out, not_4_out);
  and and_5 (and_5_out, not_2_out, C);
  and and_6 (and_6_out, C, not_4_out);
  and and_7 (and_7_out, B, not_3_out, D);
  and and_8 (and_8_out, C, D);
  and and_9 (and_9_out, not_2_out, not_4_out);
  and and_10 (and_10_out, C, not_4_out);
  and and_11 (and_11_out, not_3_out, not_4_out);
  and and_12 (and_12_out, B, not_3_out);
  and and_13 (and_13_out, B, not_4_out);
  and and_14 (and_14_out, not_2_out, C);
  and and_15 (and_15_out, C, not_4_out);
  and and_16 (and_16_out, B, not_3_out);
  or or_1 (a_2, C, A, and_1_out, and_2_out);
  or or_2 (b_2, not_2_out, and_8_out, and_3_out);
  or or_3 (c_2, not_3_out, D, B);
  or or_4 (d_2, A, and_4_out, and_5_out, and_6_out, and_7_out);
  or or_5 (e, and_9_out, and_10_out);
  or or_6 (f, A, and_11_out, and_12_out, and_13_out);
  or or_7 (g, A, and_14_out, and_15_out, and_16_out);
endmodule

module base_10_up_down_counter (
  input  in_1,
  input  in_2,
  output out_3,
  output out_4,
  output out_5,
  output out_6
);

  wire and_1_out, and_2_out, and_3_out, and_4_out, and_5_out, and_6_out, and_7_out, and_8_out, j_k_ff_1_qn,
       j_k_ff_2_qn, j_k_ff_3_qn, not_1_out, not_2_out, not_3_out, or_1_out, or_2_out, or_3_out, or_4_out,
       or_5_out;

  and and_1 (and_1_out, out_5, out_6, out_4, out_3);
  not not_1 (not_1_out, out_5);
  and and_2 (and_2_out, out_6, not_1_out, not_2_out, out_4);
  not not_2 (not_2_out, out_3);
  J_K_Flip_Flop j_k_ff_1 (
    .J(1'b1), .clk(in_2), .K(1'b1), .Q(out_3), .Qn(j_k_ff_1_qn), .preset(and_1_out), .reset(and_2_out));  // open: en
  not not_3 (not_3_out, in_1);
  and and_3 (and_3_out, in_1, out_3);
  and and_4 (and_4_out, j_k_ff_1_qn, not_3_out);
  or or_1 (or_1_out, and_3_out, and_4_out);
  J_K_Flip_Flop j_k_ff_2 (
    .J(or_1_out), .clk(in_2), .K(or_1_out), .Q(out_4), .Qn(j_k_ff_2_qn), .reset(or_2_out));  // open: preset, en
  or or_2 (or_2_out, and_1_out, and_2_out);
  and and_5 (and_5_out, and_3_out, out_4);
  and and_6 (and_6_out, j_k_ff_2_qn, and_4_out);
  or or_3 (or_3_out, and_5_out, and_6_out);
  or or_4 (or_4_out, and_1_out, and_2_out);
  J_K_Flip_Flop j_k_ff_3 (
    .J(or_3_out), .clk(in_2), .K(or_3_out), .Q(out_5), .Qn(j_k_ff_3_qn), .reset(or_4_out));  // open: preset, en
  and and_7 (and_7_out, and_5_out, out_5);
  or or_5 (or_5_out, and_7_out, and_8_out);
  and and_8 (and_8_out, j_k_ff_3_qn, and_6_out);
  J_K_Flip_Flop j_k_ff_4 (
    .J(or_5_out), .clk(in_2), .K(or_5_out), .Q(out_6), .preset(and_1_out), .reset(and_2_out));  // open: Qn, en
endmodule

module base_6_up_down_counter (
  input  in_1,
  input  in_2,
  output out_3,
  output out_4,
  output out_5,
  output out_6
);

  wire and_1_out, and_2_out, and_3_out, and_4_out, and_5_out, and_6_out, j_k_ff_1_qn, j_k_ff_2_qn, not_1_out,
       not_2_out, or_1_out, or_2_out, or_3_out;

  and and_1 (and_1_out, out_6, out_5, out_4, not_1_out);
  not not_1 (not_1_out, in_1);
  and and_2 (and_2_out, out_6, out_5, in_1);
  J_K_Flip_Flop j_k_ff_1 (
    .J(1'b1), .clk(in_2), .K(1'b1), .Q(out_4), .Qn(j_k_ff_1_qn), .preset(and_1_out), .reset(and_2_out));  // open: en
  not not_2 (not_2_out, in_1);
  and and_3 (and_3_out, in_1, out_4);
  and and_4 (and_4_out, j_k_ff_1_qn, not_2_out);
  or or_1 (or_1_out, and_3_out, and_4_out);
  J_K_Flip_Flop j_k_ff_2 (
    .J(or_1_out), .clk(in_2), .K(or_1_out), .Q(out_5), .Qn(j_k_ff_2_qn), .reset(or_2_out));  // open: preset, en
  or or_2 (or_2_out, and_2_out, and_1_out);
  and and_5 (and_5_out, and_3_out, out_5);
  and and_6 (and_6_out, j_k_ff_2_qn, and_4_out);
  or or_3 (or_3_out, and_5_out, and_6_out);
  J_K_Flip_Flop j_k_ff_3 (
    .J(or_3_out), .clk(in_2), .K(or_3_out), .Q(out_6), .preset(and_1_out), .reset(and_2_out));  // open: Qn, en

  assign out_3 = 1'b0;
endmodule

module base_10_to_base_6_counter (
  input  in_1,
  output out_2,
  output out_3,
  output out_4,
  output out_5,
  output out_6,
  output out_7,
  output out_8,
  output out_9
);

  wire and_1_out, and_2_out, clock_1_out, not_1_out, not_2_out, not_3_out, not_4_out, not_5_out, not_6_out,
       not_7_out, not_8_out, xor_1_out;

  Clock clock_1 (.out(clock_1_out));
  base_10_up_down_counter base_10_up_down_counter_1 (
    .out_3(out_7), .out_4(out_6), .out_5(out_4), .out_6(out_2), .in_1(in_1), .in_2(clock_1_out));
  not not_1 (not_1_out, out_4);
  not not_2 (not_2_out, out_6);
  not not_3 (not_3_out, out_2);
  not not_4 (not_4_out, out_4);
  not not_5 (not_5_out, out_6);
  not not_6 (not_6_out, out_7);
  not not_7 (not_7_out, in_1);
  and and_1 (and_1_out, in_1, out_2, not_1_out, not_2_out, out_7);
  and and_2 (and_2_out, not_3_out, not_4_out, not_5_out, not_6_out, not_7_out);
  not not_8 (not_8_out, and_2_out);
  xor xor_1 (xor_1_out, and_1_out, not_8_out);
  base_6_up_down_counter base_6_up_down_counter_1 (
    .out_3(out_3), .out_4(out_9), .out_5(out_8), .out_6(out_5), .in_1(in_1), .in_2(xor_1_out));
endmodule

module test (
  input  in_1,
  input  in_2,
  output out_3,
  output out_4,
  output out_5,
  output out_6
);

  wire and_1_out, and_2_out, and_3_out, and_4_out, and_5_out, and_6_out, j_k_ff_1_qn, j_k_ff_2_qn, not_1_out,
       not_2_out, or_1_out, or_2_out, or_3_out;

  and and_1 (and_1_out, out_6, out_5, out_4, not_1_out);
  not not_1 (not_1_out, in_1);
  and and_2 (and_2_out, out_6, out_5, in_1);
  J_K_Flip_Flop j_k_ff_1 (
    .J(1'b1), .clk(in_2), .K(1'b1), .Q(out_4), .Qn(j_k_ff_1_qn), .preset(and_1_out), .reset(and_2_out));  // open: en
  not not_2 (not_2_out, in_1);
  and and_3 (and_3_out, in_1, out_4);
  and and_4 (and_4_out, j_k_ff_1_qn, not_2_out);
  or or_1 (or_1_out, and_3_out, and_4_out);
  or or_2 (or_2_out, and_2_out, and_1_out);
  J_K_Flip_Flop j_k_ff_2 (
    .J(or_1_out), .clk(in_2), .K(or_1_out), .Q(out_5), .Qn(j_k_ff_2_qn), .reset(or_2_out));  // open: preset, en
  and and_5 (and_5_out, and_3_out, out_5);
  or or_3 (or_3_out, and_5_out, and_6_out);
  and and_6 (and_6_out, j_k_ff_2_qn, and_4_out);
  J_K_Flip_Flop j_k_ff_3 (
    .J(or_3_out), .clk(in_2), .K(or_3_out), .Q(out_6), .preset(and_1_out), .reset(and_2_out));  // open: Qn, en

  assign out_3 = 1'b0;
endmodule

module test_2 (
  input  in_1,
  input  in_2,
  output out_3,
  output out_4,
  output out_5,
  output out_6
);

  wire and_1_out, and_2_out, and_3_out, and_4_out, and_5_out, and_6_out, and_7_out, and_8_out, j_k_ff_1_qn,
       j_k_ff_2_qn, j_k_ff_3_qn, not_1_out, not_2_out, not_3_out, or_1_out, or_2_out, or_3_out, or_4_out,
       or_5_out;

  and and_1 (and_1_out, out_5, out_6, out_4, out_3);
  and and_2 (and_2_out, out_6, not_1_out, not_2_out, out_4);
  not not_1 (not_1_out, out_5);
  not not_2 (not_2_out, out_3);
  J_K_Flip_Flop j_k_ff_1 (
    .J(1'b1), .clk(in_2), .K(1'b1), .Q(out_3), .Qn(j_k_ff_1_qn), .preset(and_1_out), .reset(and_2_out));  // open: en
  not not_3 (not_3_out, in_1);
  and and_3 (and_3_out, in_1, out_3);
  and and_4 (and_4_out, j_k_ff_1_qn, not_3_out);
  or or_1 (or_1_out, and_3_out, and_4_out);
  or or_2 (or_2_out, and_1_out, and_2_out);
  J_K_Flip_Flop j_k_ff_2 (
    .J(or_1_out), .clk(in_2), .K(or_1_out), .Q(out_4), .Qn(j_k_ff_2_qn), .reset(or_2_out));  // open: preset, en
  and and_5 (and_5_out, and_3_out, out_4);
  or or_3 (or_3_out, and_5_out, and_6_out);
  and and_6 (and_6_out, j_k_ff_2_qn, and_4_out);
  J_K_Flip_Flop j_k_ff_3 (
    .J(or_3_out), .clk(in_2), .K(or_3_out), .Q(out_5), .Qn(j_k_ff_3_qn), .reset(or_4_out));  // open: preset, en
  or or_4 (or_4_out, and_1_out, and_2_out);
  and and_7 (and_7_out, and_5_out, out_5);
  and and_8 (and_8_out, j_k_ff_3_qn, and_6_out);
  or or_5 (or_5_out, and_7_out, and_8_out);
  J_K_Flip_Flop j_k_ff_4 (
    .J(or_5_out), .clk(in_2), .K(or_5_out), .Q(out_6), .preset(and_1_out), .reset(and_2_out));  // open: Qn, en
endmodule
